# Fritzing sketch AQ_Board (saved by Fritzing 0.8.7b)
circuit board: 6.23058cm x 5.75983cm
breadboards: 1

parts:
  part = Resistor [tolerance=±5% resistance=4.7k package=THT]
  part_2 = female pin header, 3 pins [form="♀ (female)"]
  part_3 = female pin header, 3 pins [form="♀ (female)"]
  part_4 = female pin header, 6 pins [form="♀ (female)"]
  part_5 = female pin header, 4 pins [form="♀ (female)"]
  part_6 = female pin header, 11 pins [form="♀ (female)"]
  part_7 = female pin header, 6 pins [form="♀ (female)"]
  part_8 = female pin header, 3 pins [form="♀ (female)"]

nets:
  N1: part.Pin_0, part_2.pin2, part_3.pin2, part_8.pin2
  N2: part.Pin_1, part_2.pin1, part_3.pin1, part_4.pin1, part_6.pin10, part_8.pin3
  N3: part_2.pin3, part_3.pin3, part_8.pin1
  N4: part_4.pin2, part_5.pin4
  N5: part_4.pin3, part_5.pin3
  N6: part_4.pin4, part_5.pin2
  N7: part_4.pin5, part_5.pin1
  N8: part_6.pin3, part_7.pin6
  N9: part_6.pin4, part_7.pin5
  N10: part_6.pin5, part_7.pin4
  N11: part_6.pin6, part_7.pin3
  N12: part_6.pin7, part_7.pin2
  N13: part_6.pin8, part_6.pin11
  N14: part_6.pin9, part_7.pin1

notes:
  5v - Relays
  Power + Sensor
  4.7k Ohm
  DS18B20_1
  DS18B20_2
  Relays
  Display
  Data LCD
