# Fritzing sketch Anti_Reset (saved by Fritzing 0.8.7b)
circuit board: 1.64769cm x 2.14697cm
breadboards: 1

parts:
  C1 = Electrolytic Capacitor [capacitance=10µF voltage=16V package="100 mil [THT, electrolytic]"]
  J1 = female pin header, 1 pin [form="♀ (female)"]
  J2 = female pin header, 2 pins [form="♀ (female)"]
  J4 = female pin header, 1 pin [form="♀ (female)"]

nets:
  N1: C1.-, J4.pin1
  N2: C1.+, J2.pin1
  N3: J1.pin1, J2.pin2
