# Fritzing sketch LCD_Adapter (saved by Fritzing 0.8.7b)
circuit board: 8.46667cm x 5.64444cm
circuit board: 8.03568cm x 3.61815cm
breadboards: 1

parts:
  part = Trimmer Potentiometer [maximum_resistance=10kΩ package=THT]
  part_2 = female pin header, 11 pins [form="♀ (female)"]
  part_3 = female pin header, 16 pins [form="♀ (female)"]

nets:
  N1: part.leg1, part_2.pin10, part_3.pin15
  N2: part.wiper, part_3.pin14
  N3: part.leg2, part_2.pin11, part_3.pin16
  N4: part_2.pin1, part_3.pin1
  N5: part_2.pin2, part_3.pin2
  N6: part_2.pin3, part_3.pin3
  N7: part_2.pin4, part_3.pin4
  N8: part_2.pin5, part_3.pin5
  N9: part_2.pin6, part_3.pin6
  N10: part_2.pin7, part_3.pin11
  N11: part_2.pin8, part_3.pin12
  N12: part_2.pin9, part_3.pin13
