# Fritzing sketch Untitled Sketch (saved by Fritzing 0.8.7b)
circuit board: 8.14405cm x 3.33478cm
breadboards: 1

parts:
  Pad1 = Pad [width=5.39405898692811 height=5.6430668006536 connect=center]
  Pad2 = Pad [width=5.39405898692811 height=5.6430668006536 connect=center]
  R1 = Resistor [tolerance=±5% resistance=4.7k package=THT]
  C1 = Electrolytic Capacitor [capacitance=0.47mF package="100 mil [THT, electrolytic]"]
  R2 = Resistor [tolerance=±5% resistance=220 package=THT]
  Q1 = NPN-Transistor [package="TO92 [THT]"]
  Pad3 = Pad [width=5.39405898692811 height=5.6430668006536 connect=center]
  Pad4 = Pad [width=5.39405898692811 height=5.6430668006536 connect=center]
  R3 = Resistor [tolerance=±5% resistance=220 package=THT]
  Pad5 = Pad [width=5.39405898692811 height=5.6430668006536 connect=center]

nets:
  N1: Pad1.pad, R1.Pin_0
  N2: Pad2.pad, C1.+, R2.Pin_1, Pad4.pad
  N3: R1.Pin_1, C1.-, R2.Pin_0, Q1.B
  N4: Q1.E, Pad5.pad
  N5: Q1.C, R3.Pin_0
  N6: Pad3.pad, R3.Pin_1

notes:
  4.7 KOhm
  470 uF
  33 KOhm
  47 Ohm
  +
  GND
  -
  Switch
  12V
