# Fritzing sketch Status_LED_Board (saved by Fritzing 0.8.7b)
circuit board: 1.67243cm x 2.8176cm
breadboards: 1

parts:
  LED1 = LED - 5mm [color="Red (633nm)" package="5 mm [THT]"]
  LED2 = LED - 5mm [color="Red (633nm)" package="5 mm [THT]"]
  LED3 = LED - 5mm [color="Red (633nm)" package="5 mm [THT]"]
  J1 = female pin header, 4 pins [form="♀ (female)"]
  R1 = Resistor [tolerance=±5% resistance=220 package=THT]
  R2 = Resistor [tolerance=±5% resistance=220 package=THT]

nets:
  N1: LED1.cathode, LED2.cathode, LED3.cathode, J1.pin4
  N2: LED1.anode, J1.pin1
  N3: LED2.anode, R1.Pin_1
  N4: LED3.anode, R2.Pin_1
  N5: J1.pin2, R1.Pin_0
  N6: J1.pin3, R2.Pin_0
